// Logisim project exp6-1b.circ as structural Verilog: 1 circuit, main circuit main
module main (
  input  [2:0] A___B___C,
  output out_2
);

  wire decoder_1_out0, decoder_1_out2, decoder_1_out4;

  Decoder #(.select(3), .tristate("false")) decoder_1 (
    .out0(decoder_1_out0), .out2(decoder_1_out2), .out4(decoder_1_out4), .sel(A___B___C));  // open: out1, out3, out5, out6, out7
  or or_1 (out_2, decoder_1_out0, decoder_1_out2, decoder_1_out4);

  // Notes on the sheet:
  //   Fernando Flores
  //   Section 5
  //   Experiment 6
  //   Activity 1b
endmodule
