// Logisim project exp6-2a.circ as structural Verilog: 1 circuit, main circuit main
module main (
);

  wire and_1_out, and_2_out, bcd_to_7_segment_decoder_1_p5, bcd_to_7_segment_decoder_1_p6,
       bcd_to_7_segment_decoder_1_p7, bcd_to_7_segment_decoder_1_p8, bcd_to_7_segment_decoder_1_p9,
       bcd_to_7_segment_decoder_1_p10, bcd_to_7_segment_decoder_1_p11, bcd_to_7_segment_decoder_1_p12,
       button_1_out, button_2_out, j_k_ff_1_q, j_k_ff_2_q, j_k_ff_3_q, j_k_ff_3_qn;

  J_K_Flip_Flop #(.trigger("rising")) j_k_ff_1 (
    .J(1'b1), .clk(button_1_out), .K(1'b1), .Q(j_k_ff_1_q), .reset(button_2_out));  // open: Qn, preset, en
  Button button_1 (.out(button_1_out));
  Button button_2 (.out(button_2_out));
  J_K_Flip_Flop #(.trigger("rising")) j_k_ff_2 (
    .J(j_k_ff_1_q), .clk(button_1_out), .K(j_k_ff_1_q), .Q(j_k_ff_2_q), .reset(button_2_out));  // open: Qn, preset, en
  and and_1 (and_1_out, j_k_ff_1_q, j_k_ff_2_q);
  and and_2 (and_2_out, and_1_out, j_k_ff_3_q);
  J_K_Flip_Flop #(.trigger("rising")) j_k_ff_3 (
    .J(and_1_out), .clk(button_1_out), .K(and_1_out), .Q(j_k_ff_3_q), .Qn(j_k_ff_3_qn), .reset(button_2_out));  // open: preset, en
  // BCD_to_7_segment_decoder bcd_to_7_segment_decoder_1: pin names not known; wires that end beside it: j_k_ff_3_qn, j_k_ff_1_q, j_k_ff_2_q, j_k_ff_3_q, bcd_to_7_segment_decoder_1_p5, bcd_to_7_segment_decoder_1_p6, bcd_to_7_segment_decoder_1_p7, bcd_to_7_segment_decoder_1_p8, bcd_to_7_segment_decoder_1_p9, bcd_to_7_segment_decoder_1_p10, bcd_to_7_segment_decoder_1_p11, bcd_to_7_segment_decoder_1_p12
  J_K_Flip_Flop #(.trigger("rising")) j_k_ff_4 (
    .J(and_2_out), .clk(button_1_out), .K(and_2_out), .Q(bcd_to_7_segment_decoder_1_p5), .reset(button_2_out));  // open: Qn, preset, en
  _7_Segment_Display u_7_segment_display_1 (
    .g(bcd_to_7_segment_decoder_1_p12), .f(bcd_to_7_segment_decoder_1_p11),
    .a(bcd_to_7_segment_decoder_1_p6), .b(bcd_to_7_segment_decoder_1_p7), .e(bcd_to_7_segment_decoder_1_p10),
    .d(bcd_to_7_segment_decoder_1_p9), .c(bcd_to_7_segment_decoder_1_p8));  // open: dp

  // Notes on the sheet:
  //   Section 5
  //   Fernando Flores
  //   Experiment 6
  //   Excercise 2a
endmodule
